# Fritzing sketch WSODFix (saved by Fritzing 0.9.6b)
breadboards: 1

parts:
  U1 = RJ45 Jack [package=rj45-8]
  M1 = STM32F103C8T6 blue mini board
  R1 = Resistor [tolerance=±5% power=0.25 resistance=1k package=THT]
  R2 = Resistor [tolerance=±5% power=0.25 resistance=10k package=THT]
  R3 = Resistor [tolerance=±5% power=0.25 resistance=68 package=THT]
  LED1 = LED - 3mm [color="Green (560nm)" current=0.030 package="3 mm [THT]"]

nets:
  3V: U1.1, R1.Pin_1, R2.Pin_1
  GND: U1.2, U1.3, M1.G, M1.GND, R2.Pin_0
  N1: U1.4, M1.B10
  N2: U1.5, M1.B11
  N3: U1.6, M1.B1
  5V: U1.8, M1.5V
  N4: M1.B12, R3.Pin_0
  3.3V: M1.3.3V, R1.Pin_0, LED1.anode
  N5: R3.Pin_1, LED1.cathode

notes:
  WSODFix, A repair tool for Symbian Nokia phones affected by the infamous white screen of death., 1
